# Fritzing sketch aPCmeter_sch (saved by Fritzing 0.9.2b)
breadboards: 1

parts:
  Arduino_Nano_3_0 = Arduino Nano (Rev3.0)
  R1 = Resistor [tolerance=±5% resistance=220 package=THT]
  LED_CPU = RGB LED (com. anode, rbg) [package="5 mm [THT]"]
  R2 = Resistor [tolerance=±5% resistance=100 package=THT]
  R3 = Resistor [tolerance=±5% resistance=100 package=THT]
  LED_RAM = RGB LED (com. anode, rbg) [package="5 mm [THT]"]
  R4 = Resistor [tolerance=±5% resistance=220 package=THT]
  R5 = Resistor [tolerance=±5% resistance=100 package=THT]
  R6 = Resistor [tolerance=±5% resistance=100 package=THT]
  GAUGE_CPU = Header 2 [package=molex-1x2_lock]
  C1 = Electrolytic Capacitor [capacitance=100μF voltage=10V package="0807 [SMD, electrolytic]"]
  R7 = Resistor [tolerance=±5% resistance=220 package=THT]
  D1 = Rectifier Diode [part_number=1N4001 package="300 mil [THT]"]
  GAUGE_RAM = Header 2 [package=molex-1x2_lock]
  R8 = Resistor [tolerance=±5% resistance=220 package=THT]
  C2 = Electrolytic Capacitor [capacitance=100μF voltage=10V package="0807 [SMD, electrolytic]"]
  D2 = Rectifier Diode [part_number=1N4001 package="300 mil [THT]"]

nets:
  GND: Arduino_Nano_3_0.GND, GAUGE_CPU.2, C1.-, D1.anode, GAUGE_RAM.2, C2.-, D2.anode
  N1: Arduino_Nano_3_0.D2, R3.Pin_0
  N2: Arduino_Nano_3_0.D3, R1.Pin_0
  N3: Arduino_Nano_3_0.D5, R2.Pin_0
  N4: Arduino_Nano_3_0.D6, R7.Pin_0
  N5: Arduino_Nano_3_0.D9, R4.Pin_0
  N6: Arduino_Nano_3_0.D10, R5.Pin_0
  N7: Arduino_Nano_3_0.D11/MOSI, R8.Pin_0
  5V: Arduino_Nano_3_0.5V, LED_CPU.common_anode, LED_RAM.common_anode
  N8: Arduino_Nano_3_0.A5, R6.Pin_1
  N9: R1.Pin_1, LED_CPU.red_cathode
  N10: LED_CPU.blue_cathode, R3.Pin_1
  N11: LED_CPU.green_cathode, R2.Pin_1
  N12: LED_RAM.red_cathode, R4.Pin_1
  N13: LED_RAM.blue_cathode, R6.Pin_0
  N14: LED_RAM.green_cathode, R5.Pin_1
  N15: GAUGE_CPU.1, C1.+, R7.Pin_1, D1.cathode
  N16: GAUGE_RAM.1, R8.Pin_1, C2.+, D2.cathode

notes:
  Diodes should be placed close to gauges as much as possible.
  CPU SIDE
  RAM SIDE
